# Fritzing sketch pomoduino2_only_leds (saved by Fritzing 0.9.2b)
breadboards: 1

parts:
  J1 = Piezo Speaker
  B1 = Pushbutton [package="[THT]"]
  B2 = Pushbutton [package="[THT]"]
  Part1 = Arduino Nano (Rev3.0)
  R1 = Resistor [tolerance=±5% resistance=1k package=THT]
  R3 = Resistor [tolerance=±5% resistance=1k package=THT]
  R4 = Resistor [tolerance=±5% resistance=1k package=THT]
  R5 = Resistor [tolerance=±5% resistance=1k package=THT]
  R2 = Resistor [tolerance=±5% resistance=1k package=THT]
  LED1 = LED - 3mm [color="Red (633nm)" package="3 mm [THT]"]
  LED2 = LED - 3mm [color="Red (633nm)" package="3 mm [THT]"]
  LED3 = LED - 3mm [color="Red (633nm)" package="3 mm [THT]"]
  LED4 = LED - 3mm [color="Red (633nm)" package="3 mm [THT]"]
  LED5 = LED - 3mm [color="Red (633nm)" package="3 mm [THT]"]

nets:
  N1: J1.pin1, B1.Pin_3, B1.Pin_4, B2.Pin_3, B2.Pin_4, Part1.GND, LED1.cathode, LED2.cathode, LED3.cathode, LED4.cathode, LED5.cathode
  N2: J1.pin2, Part1.D2
  N3: B1.Pin_1, B1.Pin_2, Part1.D3
  N4: B2.Pin_1, B2.Pin_2, Part1.D4
  N5: Part1.D5, R1.Pin_0
  N6: Part1.D6, R2.Pin_0
  N7: Part1.D7, R3.Pin_0
  N8: Part1.D8, R4.Pin_0
  N9: Part1.D9, R5.Pin_0
  N10: R1.Pin_1, LED1.anode
  N11: R3.Pin_1, LED3.anode
  N12: R4.Pin_1, LED4.anode
  N13: R5.Pin_1, LED5.anode
  N14: R2.Pin_1, LED2.anode
