# Fritzing sketch pomoduino2_sketch (saved by Fritzing 0.9.2b)
breadboards: 1

parts:
  Part1 = Arduino Uno (Rev3)
  LCD1 = LCD screen
  J1 = Piezo Speaker
  R1 = Trimmer Potentiometer [maximum_resistance=10kΩ package=THT]
  R2 = Resistor [tolerance=±5% resistance=220 package=THT]
  B1 = Pushbutton [package="[THT]"]
  B2 = Pushbutton [package="[THT]"]

nets:
  N1: Part1.D8, LCD1.RS
  N2: Part1.D9_PWM, LCD1.E
  N3: Part1.D10_PWM/SS, LCD1.DB4
  N4: Part1.D11_PWM/MOSI, LCD1.DB5
  N5: Part1.D12/MISO, LCD1.DB6
  N6: Part1.D13/SCK, LCD1.DB7
  GND: Part1.GND, LCD1.VSS, LCD1.R/W, LCD1.LED-, J1.pin1, R1.leg2, B1.Pin_3, B1.Pin_4, B2.Pin_3, B2.Pin_4
  N7: Part1.D2, J1.pin2
  N8: Part1.D3_PWM, B1.Pin_1, B1.Pin_2
  N9: Part1.D5_PWM, B2.Pin_1, B2.Pin_2
  5V: Part1.5V, LCD1.VDD, R1.leg1, R2.Pin_0
  N10: LCD1.V0, R1.wiper
  N11: LCD1.LED+, R2.Pin_1
