# Fritzing sketch nano (saved by Fritzing 0.9.2b)
breadboards: 1

parts:
  Part1 = Arduino Nano (Rev3.0)
  LCD1 = LCD screen
  S1 = Pushbutton [package="[THT]"]
  S2 = Pushbutton [package="[THT]"]
  J1 = Piezo Speaker
  C1 = Electrolytic Capacitor [capacitance=0.1mF package="100 mil [THT, electrolytic]"]

nets:
  GND: Part1.GND, LCD1.VSS, LCD1.R/W, LCD1.LED-, S1.Pin_1, S1.Pin_2, S2.Pin_1, S2.Pin_2, J1.pin1, C1.-
  N1: Part1.D2, J1.pin2
  N2: Part1.D3, S2.Pin_3, S2.Pin_4
  N3: Part1.D4, S1.Pin_3, S1.Pin_4
  N4: Part1.D5, LCD1.V0, C1.+
  N5: Part1.D6, LCD1.LED+
  N6: Part1.D7, LCD1.RS
  N7: Part1.D8, LCD1.E
  N8: Part1.D9, LCD1.DB4
  N9: Part1.D10, LCD1.DB5
  N10: Part1.D11/MOSI, LCD1.DB6
  N11: Part1.D12/MISO, LCD1.DB7
  5V: Part1.5V, LCD1.VDD
